# Fritzing sketch RpiV2 (saved by Fritzing 0.9.3b)
circuit board: 6.5cm x 3cm
breadboards: 1

parts:
  Mazkeka = Raspberry Pi Zero
  Q1 = MOSFET-NCHANNEL [package=sot23-3]
  U1 = AUDIO-JACK2 [package=audio-jack]
  R1 = Resistor [tolerance=±5% resistance=10k package="0805 [SMD]"]
  R2 = Resistor [tolerance=±5% resistance=4.7k package="0805 [SMD]"]
  LED1 = smd LED [color="Green (570nm)" package="0805 [SMD]"]
  R3 = Resistor [tolerance=±5% resistance=100 package="0805 [SMD]"]
  Solenoid = screw terminal, 3 pins
  HP = screw terminal, 2 pins
  J1 = screw terminal, 3 pins
  S1 = SPST Switch [package=switch-spdt-smd]
  Q2 = MOSFET-NCHANNEL [package=sot23-3]
  Q3 = MOSFET-NCHANNEL [package=sot23-3]
  R4 = Resistor [tolerance=±5% resistance=10k package="0805 [SMD]"]
  R5 = Resistor [tolerance=±5% resistance=10k package="0805 [SMD]"]
  I2C = female pin header, 4 pins [form="♀ (female)"]
  I2C_2 = female pin header, 4 pins [form="♀ (female)"]
  R6 = Resistor [tolerance=±5% resistance=10k package="0805 [SMD]"]
  S2 = Pushbutton [package="[THT]"]
  R7 = Resistor [tolerance=±5% resistance=5k package="0805 [SMD]"]
  R8 = Resistor [tolerance=±5% resistance=5k package="0805 [SMD]"]
  PullUp = SPST Switch [package=switch-spdt-smd]

nets (from the pcb view):
  N1: Mazkeka.pin_1, Mazkeka.pin_17, U1.SLEEVE, R2.Pin_1, R3.Pin_1, I2C.pin2, I2C_2.pin2, R6.Pin_0
  N2: Mazkeka.pin_2, J1.pin2, S1.S
  N3: Mazkeka.pin_3, I2C.pin4, I2C_2.pin4, R8.Pin_0
  N4: Mazkeka.pin_5, I2C.pin3, I2C_2.pin3, R7.Pin_0
  N5: Mazkeka.pin_6, Mazkeka.pin_9, Mazkeka.pin_25, Mazkeka.pin_39, Q1.D, U1.TIP, R1.Pin_1, J1.pin1, I2C.pin1, I2C_2.pin1
  N6: Mazkeka.pin_7, U1.RING, R2.Pin_0
  N7: Mazkeka.pin_15, S2.Pin_1, S2.Pin_2
  N8: Mazkeka.pin_29, Q1.G, R1.Pin_0
  N9: Mazkeka.pin_35, R5.Pin_1
  N10: Mazkeka.pin_37, R4.Pin_1
  N11: Q1.S, LED1.cathode, HP.pin2
  N12: LED1.anode, R3.Pin_0
  N13: Solenoid.pin1, Q3.S
  N14: Solenoid.pin2, S1.P
  N15: Solenoid.pin3, Q2.S
  N16: HP.pin1, J1.pin3, S1.O
  N17: Q2.G, R5.Pin_0
  N18: Q2.D, Q3.D
  N19: Q3.G, R4.Pin_0
  N20: R6.Pin_1, S2.Pin_3, S2.Pin_4, PullUp.S
  N21: R7.Pin_1, R8.Pin_1, PullUp.O, PullUp.P

notes:
  5V
  12V
  GND
  GND1
  VCC
  SCL
  SDA
  AF
  V2
